# Fritzing sketch breadboard_schematic (saved by Fritzing 0.9.3b)
breadboards: 1

parts:
  Part1 = Arduino Pro Micro (Clone)
  LCM1602_IIC1 = LCM1602 IIC [part_number="LCM1602 IIC" chip_label="LCM1602 IIC" package="DIP (Dual Inline) [THT]"]
  RE1 = Rotary Encoder [package=THT]
  LCD1 = LCD screen
  C1 = Ceramic Capacitor [capacitance=100nF package="200 mil [THT, multilayer]"]
  C2 = Ceramic Capacitor [capacitance=100nF package="200 mil [THT, multilayer]"]
  C3 = Ceramic Capacitor [capacitance=100nF package="200 mil [THT, multilayer]"]
  R1 = Resistor [tolerance=±5% resistance=15k package=THT]
  R2 = Resistor [tolerance=±5% resistance=15k package=THT]
  R3 = Resistor [tolerance=±5% resistance=15k package=THT]

nets:
  N1: Part1.TXO, R3.Pin_1
  N2: Part1.RXI, R2.Pin_1
  GND: Part1.GND, LCM1602_IIC1.GND, RE1.EncoderPinC, RE1.SwitchPinE, C1.1, C2.1, C3.0
  N3: Part1.D2, LCM1602_IIC1.SDA
  N4: Part1.D3, LCM1602_IIC1.SCL
  N5: Part1.D7, R1.Pin_1
  VCC: Part1.VCC, LCM1602_IIC1.VCC
  VSS: LCM1602_IIC1.VSS, LCD1.VSS
  VDD: LCM1602_IIC1.VDD, LCD1.VDD
  N6: LCM1602_IIC1.V0, LCD1.V0
  N7: LCM1602_IIC1.RS, LCD1.RS
  N8: LCM1602_IIC1.RW, LCD1.R/W
  N9: LCM1602_IIC1.E, LCD1.E
  N10: LCM1602_IIC1.D0, LCD1.DB0
  N11: LCM1602_IIC1.D1, LCD1.DB1
  N12: LCM1602_IIC1.D2, LCD1.DB2
  N13: LCM1602_IIC1.D3, LCD1.DB3
  N14: LCM1602_IIC1.D4, LCD1.DB4
  N15: LCM1602_IIC1.D5, LCD1.DB5
  N16: LCM1602_IIC1.D6, LCD1.DB6
  N17: LCM1602_IIC1.D7, LCD1.DB7
  N18: LCM1602_IIC1.A, LCD1.LED+
  N19: LCM1602_IIC1.K, LCD1.LED-
  N20: LCM1602_IIC1.LED_A, LCM1602_IIC1.LED_B
  N21: RE1.EncoderPinA, C1.0, R3.Pin_0
  N22: RE1.EncoderPinB, C2.0, R2.Pin_0
  N23: C3.1, R1.Pin_0

custom parts:
  LCM1602 IIC: I2C-Module to use a 1602 or 2004 LCD on with the wire.h libory Serial LCD Modul
  Rotary Encoder: Rotary Encoder from ALPSec11e with switch.
